// Logisim project SNES_controller.circ as structural Verilog: 2 circuits, main circuit main
module main (
  input  RIGHT,
  input  LEFT,
  input  DOWN,
  input  UP,
  input  R,
  input  START,
  input  L,
  input  SEL,
  input  X,
  input  Y,
  input  A,
  input  B,
  input  SNES_LATCH,
  output SNES_OUT
);

  wire cd4021b_1_q7, SNES_CLOCK_out;

  Clock SNES_CLOCK (.out(SNES_CLOCK_out));
  CD4021B cd4021b_1 (
    .D0(1'b1), .D1(1'b1), .D2(1'b1), .D3(1'b1), .D4(R), .D5(L), .D6(X), .D7(A), .DS(1'b1), .PL(SNES_LATCH),
    .CLK(SNES_CLOCK_out), .Q7(cd4021b_1_q7));  // open: Q5, Q6
  CD4021B cd4021b_2 (
    .D0(RIGHT), .D1(LEFT), .D2(DOWN), .D3(UP), .D4(START), .D5(SEL), .D6(Y), .D7(B), .DS(cd4021b_1_q7),
    .PL(SNES_LATCH), .CLK(SNES_CLOCK_out), .Q7(SNES_OUT));  // open: Q5, Q6

  // Notes on the sheet:
  //   R: pull=up
  //   L: pull=up
  //   X: pull=up
  //   A: pull=up
  //   RIGHT: pull=up
  //   LEFT: pull=up
  //   DOWN: pull=up
  //   UP: pull=up
  //   START: pull=up
  //   SEL: pull=up
  //   Y: pull=up
  //   B: pull=up
endmodule

module CD4021B (
  input  D0,
  input  D1,
  input  D2,
  input  D3,
  input  D4,
  input  D5,
  input  D6,
  input  D7,
  input  DS,
  input  PL,
  input  CLK,
  output Q5,
  output Q6,
  output Q7
);

  wire and_1_out, and_2_out, and_3_out, and_4_out, and_5_out, and_6_out, and_7_out, and_8_out, and_9_out,
       and_10_out, and_11_out, and_12_out, and_13_out, and_14_out, and_15_out, and_16_out, d_ff_1_q,
       d_ff_2_q, d_ff_3_q, d_ff_4_q, d_ff_5_q, nand_1_out, not_1_out, not_2_out, not_3_out, not_4_out,
       not_5_out, not_6_out, not_7_out, not_8_out, not_9_out, not_10_out, not_11_out, not_12_out, not_13_out,
       not_14_out, not_15_out, not_16_out, not_17_out, not_18_out, not_19_out;

  not not_1 (not_1_out, PL);
  not not_2 (not_2_out, not_1_out);
  not not_3 (not_3_out, CLK);
  not not_4 (not_4_out, D0);
  not not_5 (not_5_out, not_4_out);
  and and_1 (and_1_out, not_2_out, not_5_out);
  D_Flip_Flop d_ff_1 (.D(DS), .clk(nand_1_out), .Q(d_ff_1_q), .preset(and_1_out), .reset(and_2_out));  // open: Qn
  and and_2 (and_2_out, not_2_out, not_4_out);
  nand nand_1 (nand_1_out, not_1_out, not_3_out);
  not not_6 (not_6_out, D1);
  not not_7 (not_7_out, not_6_out);
  and and_3 (and_3_out, not_2_out, not_7_out);
  D_Flip_Flop d_ff_2 (.D(d_ff_1_q), .clk(nand_1_out), .Q(d_ff_2_q), .preset(and_3_out), .reset(and_4_out));  // open: Qn
  and and_4 (and_4_out, not_2_out, not_6_out);
  D_Flip_Flop d_ff_3 (.D(d_ff_2_q), .clk(nand_1_out), .Q(d_ff_3_q), .preset(and_5_out), .reset(and_6_out));  // open: Qn
  not not_8 (not_8_out, D2);
  not not_9 (not_9_out, not_8_out);
  and and_5 (and_5_out, not_2_out, not_9_out);
  and and_6 (and_6_out, not_2_out, not_8_out);
  not not_10 (not_10_out, D3);
  not not_11 (not_11_out, not_10_out);
  and and_7 (and_7_out, not_2_out, not_11_out);
  D_Flip_Flop d_ff_4 (.D(d_ff_3_q), .clk(nand_1_out), .Q(d_ff_4_q), .preset(and_7_out), .reset(and_8_out));  // open: Qn
  and and_8 (and_8_out, not_2_out, not_10_out);
  not not_12 (not_12_out, D4);
  not not_13 (not_13_out, not_12_out);
  and and_9 (and_9_out, not_2_out, not_13_out);
  D_Flip_Flop d_ff_5 (
    .D(d_ff_4_q), .clk(nand_1_out), .Q(d_ff_5_q), .preset(and_9_out), .reset(and_10_out));  // open: Qn
  and and_10 (and_10_out, not_2_out, not_12_out);
  not not_14 (not_14_out, D5);
  not not_15 (not_15_out, not_14_out);
  and and_11 (and_11_out, not_2_out, not_15_out);
  D_Flip_Flop d_ff_6 (.D(d_ff_5_q), .clk(nand_1_out), .Q(Q5), .preset(and_11_out), .reset(and_12_out));  // open: Qn
  and and_12 (and_12_out, not_2_out, not_14_out);
  not not_16 (not_16_out, D6);
  not not_17 (not_17_out, not_16_out);
  and and_13 (and_13_out, not_2_out, not_17_out);
  D_Flip_Flop d_ff_7 (.D(Q5), .clk(nand_1_out), .Q(Q6), .preset(and_13_out), .reset(and_14_out));  // open: Qn
  and and_14 (and_14_out, not_2_out, not_16_out);
  not not_18 (not_18_out, D7);
  not not_19 (not_19_out, not_18_out);
  and and_15 (and_15_out, not_2_out, not_19_out);
  D_Flip_Flop d_ff_8 (.D(Q6), .clk(nand_1_out), .Q(Q7), .preset(and_15_out), .reset(and_16_out));  // open: Qn
  and and_16 (and_16_out, not_2_out, not_18_out);
endmodule
